# Fritzing sketch open_bike_light (saved by Fritzing 0.9.9b)
breadboards: 1

parts:
  U1 = attiny85 [package=dip]
  TP1 = TP4056 [chip_label=TP4056 package="DIP (Dual Inline) [THT]"]
  U2 = LIPO-110mAh [package=lipo-110]
  S1 = Pushbutton [package="[THT]"]
  LED1 = LED - 5mm [color="Red (633nm)" current=0.030 package="5 mm [THT]"]
  R1 = Resistor [tolerance=±5% power=0.25 resistance=47 package=THT]

nets:
  N1: U1.Pin_3, S1.Pin_1, S1.Pin_2
  N2: U1.Pin_4, TP1.pin6, S1.Pin_3, S1.Pin_4, R1.Pin_1
  N3: U1.Pin_5, LED1.anode
  N4: U1.Pin_8, TP1.pin3
  N5: TP1.pin4, U2.+
  N6: TP1.pin5, U2.-
  N7: LED1.cathode, R1.Pin_0

custom parts:
  TP4056: A DIP stand-in part for whatever IC you want. With 6 pins on a 300mil dual inline package (DIP) footprint.
